# Fritzing sketch DIY_Attingy84_Synteny_V1 (saved by Fritzing 0.9.0b)
circuit board: 2.64311cm x 6.26847cm
breadboards: 1

parts:
  U1 = atmega328 [package=dip]
  Y1 = Resonator [frequency="16 Mhz" package=THT]
  LED1 = LED - 5mm [color="Red (633nm)" package="5 mm [THT]"]
  R1 = Resistor [tolerance=±5% resistance=220 package=THT]
  Power_plug1 = Power plug
  J16 = female pin header, 2 pins [form="♀ (female)"]
  J10 = female pin header, 6 pins [form="♀ (female)"]
  J13 = female pin header, 4 pins [form="♀ (female)"]
  J11 = female pin header, 5 pins [form="♀ (female)"]
  J12 = female pin header, 5 pins [form="♀ (female)"]
  J14 = female pin header, 2 pins [form="♀ (female)"]
  R2 = Resistor [tolerance=±5% resistance=220 package="0603 [SMD]"]
  LED2 = smd LED [color="Red (633nm)" package="0603 [SMD]"]
  C2 = Capacitor [part_number=.1uF package=cap-pth-small2]
  J15 = female pin header, 6 pins [form="♀ (female)"]
  J18 = female pin header, 2 pins [form="♀ (female)"]
  U2 = Voltage Regulator - 5V [package="TO220 [THT]"]
  J19 = female pin header, 2 pins [form="♀ (female)"]

nets:
  N1: U1.RESET, J15.pin6
  N2: U1.D0_(RX), J12.pin1, J15.pin4
  N3: U1.D1_(TX), J12.pin2, J15.pin5
  N4: U1.D2, J12.pin3
  N5: U1.D3_(PWM), J12.pin4
  N6: U1.D4, J12.pin5
  N7: U1.VCC, U1.AVCC, J16.pin2, J14.pin2, R2.Pin_1, J15.pin3, J18.pin2, U2.output_voltage
  GND: U1.GND, Y1.GND, R1.Pin_0, Power_plug1.GND, J16.pin1, J14.pin1, LED2.cathode, C2.1, J15.pin1, J18.pin1, U2.GND, J19.pin2
  N8: U1.XLAT1, Y1.0
  N9: U1.XLAT2, Y1.pin_1
  N10: U1.D5_(PWM), J13.pin1
  N11: U1.D6_(PWM), J13.pin2
  N12: U1.D7, J13.pin3
  N13: U1.D8, J13.pin4
  N14: U1.D9_(PWM), J11.pin5
  N15: U1.D10_(PWM), J11.pin4
  N16: U1.D11_(PWM), J11.pin3
  N17: U1.D12, J11.pin2
  N18: U1.D13, LED1.anode, J11.pin1
  N19: U1.AREF, C2.2
  N20: U1.A0, J10.pin6
  N21: U1.A1, J10.pin5
  N22: U1.A2, J10.pin4
  N23: U1.A3, J10.pin3
  N24: U1.A4, J10.pin2
  N25: U1.A5, J10.pin1
  N26: LED1.cathode, R1.Pin_1
  N27: Power_plug1.VCC, U2.input_voltage, J19.pin1
  N28: R2.Pin_0, LED2.anode

notes:
  -
  +
  A
  1
  2
  3
  4
  5
  0
  D
  10
  11
  12
  13
  9
  8
  7
  6
  5V out
  TX
  5V in
  RX
  DTR
  led
  +5v
  GND
