# Fritzing sketch diy_arduino shield_v1_l293d (saved by Fritzing 0.9.0b)
circuit board: 2.62428cm x 4.85736cm
breadboards: 1

parts:
  J19 = female pin header, 5 pins [form="♀ (female)"]
  J20 = female pin header, 4 pins [form="♀ (female)"]
  J21 = female pin header, 2 pins [form="♀ (female)"]
  J22 = female pin header, 6 pins [form="♀ (female)"]  # not connected
  J23 = female pin header, 5 pins [form="♀ (female)"]  # not connected
  J25 = female pin header, 2 pins [form="♀ (female)"]  # not connected
  J30 = female pin header, 2 pins [form="♀ (female)"]
  J31 = female pin header, 2 pins [form="♀ (female)"]
  IC1 = L293D [package=THT]
  U1 = DIODE-ZENER [package=diode-zener]  # not connected

nets:
  N1: J19.pin3, IC1.In_2
  N2: J19.pin4, IC1.In_1
  N3: J20.pin3, IC1.In_3
  N4: J20.pin4, IC1.In_4
  N5: J21.pin1, J30.pin1, J31.pin1
  N6: J21.pin2, J30.pin2, J31.pin2

notes:
  12V in
  7
  8
  0
  1
  2
  5
  6
  D
  3
  4
  9
  13
  12
  11
  10
  5V out
  +
  -
