# Fritzing sketch diy_arduino shield_v1_nrf24l01 (saved by Fritzing 0.9.0b)
circuit board: 2.62428cm x 4.85736cm
breadboards: 1

parts:
  J19 = female pin header, 5 pins [form="♀ (female)"]  # not connected
  J20 = female pin header, 4 pins [form="♀ (female)"]  # not connected
  J21 = female pin header, 2 pins [form="♀ (female)"]
  J22 = female pin header, 6 pins [form="♀ (female)"]  # not connected
  J23 = female pin header, 5 pins [form="♀ (female)"]
  REG1 = LD33 Low-Dropout Voltage Regulator
  J25 = female pin header, 2 pins [form="♀ (female)"]
  J26 = double row female pin header, 8 pins [form="♀ (female)"]
  J27 = female pin header, 2 pins [form="♀ (female)"]
  J28 = female pin header, 2 pins [form="♀ (female)"]
  J29 = female pin header, 2 pins [form="♀ (female)"]
  J30 = female pin header, 2 pins [form="♀ (female)"]
  J31 = female pin header, 2 pins [form="♀ (female)"]

nets:
  N1: J21.pin1, J30.pin1, J31.pin1
  N2: J21.pin2, J30.pin2, J31.pin2
  N3: J23.pin1, J26.pin7
  N4: J23.pin2, J26.pin8
  N5: J23.pin3, J26.pin2
  N6: J23.pin4, J26.pin3
  N7: J23.pin5, J26.pin6
  N8: REG1.GND, J25.pin2, J26.pin5, J27.pin2, J28.pin2, J29.pin2
  N9: REG1.Vout, J26.pin4, J27.pin1, J28.pin1, J29.pin1
  N10: REG1.Vin, J25.pin1

notes:
  12V in
  7
  8
  0
  1
  2
  5
  6
  D
  3
  4
  9
  13
  12
  11
  10
  5V out
  -
  +
  3.3V out
